# Fritzing sketch MQ9 (saved by Fritzing 0.9.4)
breadboards: 1

parts:
  Part2 = MQ-9 breakout  # not connected
  Part3 = Arduino Uno (Rev3)
  R1 = Resistor [tolerance=±5% resistance=220 package=THT]
  LED1 = LED - 5mm [color="Red (633nm)" package="5 mm [THT]"]

nets:
  N1: Part3.D2, LED1.anode
  N2: R1.Pin_0, LED1.cathode

custom parts:
  MQ-9 breakout: SKU: 101284
